// Logisim project HalfAdder.circ as structural Verilog: 1 circuit, main circuit Half Adder
module Half_Adder (
  input  A,
  input  B,
  output S,
  output C
);

  xor xor_1 (S, A, B);
  and and_1 (C, A, B);

  // Notes on the sheet:
  //   B: pull=down
  //   S: pull=down
  //   A: pull=down
  //   C: pull=down
endmodule
