// Logisim project 20BitIncrementer.circ as structural Verilog: 1 circuit, main circuit 20BitIncrementer
module _20BitIncrementer (
  input  [19:0] I,
  output [19:0] S,
  output Overflow
);

  wire half_adder_1_c, half_adder_2_c, half_adder_3_c, half_adder_4_c, half_adder_5_c, half_adder_6_c,
       half_adder_7_c, half_adder_8_c, half_adder_9_c, half_adder_10_c, half_adder_11_c, half_adder_12_c,
       half_adder_13_c, half_adder_14_c, half_adder_15_c, half_adder_16_c, half_adder_17_c, half_adder_18_c,
       half_adder_19_c;

  Half_Adder half_adder_1 (.A(1'b1), .B(I[0]), .S(S[0]), .C(half_adder_1_c));
  Half_Adder half_adder_2 (.A(half_adder_1_c), .B(I[1]), .S(S[1]), .C(half_adder_2_c));
  Half_Adder half_adder_3 (.A(half_adder_2_c), .B(I[2]), .S(S[2]), .C(half_adder_3_c));
  Half_Adder half_adder_4 (.A(half_adder_3_c), .B(I[3]), .S(S[3]), .C(half_adder_4_c));
  Half_Adder half_adder_5 (.A(half_adder_4_c), .B(I[4]), .S(S[4]), .C(half_adder_5_c));
  Half_Adder half_adder_6 (.A(half_adder_5_c), .B(I[5]), .S(S[5]), .C(half_adder_6_c));
  Half_Adder half_adder_7 (.A(half_adder_6_c), .B(I[6]), .S(S[6]), .C(half_adder_7_c));
  Half_Adder half_adder_8 (.A(half_adder_7_c), .B(I[7]), .S(S[7]), .C(half_adder_8_c));
  Half_Adder half_adder_9 (.A(half_adder_8_c), .B(I[8]), .S(S[8]), .C(half_adder_9_c));
  Half_Adder half_adder_10 (.A(half_adder_9_c), .B(I[9]), .S(S[9]), .C(half_adder_10_c));
  Half_Adder half_adder_11 (.A(half_adder_10_c), .B(I[10]), .S(S[10]), .C(half_adder_11_c));
  Half_Adder half_adder_12 (.A(half_adder_11_c), .B(I[11]), .S(S[11]), .C(half_adder_12_c));
  Half_Adder half_adder_13 (.A(half_adder_12_c), .B(I[12]), .S(S[12]), .C(half_adder_13_c));
  Half_Adder half_adder_14 (.A(half_adder_13_c), .B(I[13]), .S(S[13]), .C(half_adder_14_c));
  Half_Adder half_adder_15 (.A(half_adder_14_c), .B(I[14]), .S(S[14]), .C(half_adder_15_c));
  Half_Adder half_adder_16 (.A(half_adder_15_c), .B(I[15]), .S(S[15]), .C(half_adder_16_c));
  Half_Adder half_adder_17 (.A(half_adder_16_c), .B(I[16]), .S(S[16]), .C(half_adder_17_c));
  Half_Adder half_adder_18 (.A(half_adder_17_c), .B(I[17]), .S(S[17]), .C(half_adder_18_c));
  Half_Adder half_adder_19 (.A(half_adder_18_c), .B(I[18]), .S(S[18]), .C(half_adder_19_c));
  Half_Adder half_adder_20 (.A(half_adder_19_c), .B(I[19]), .S(S[19]), .C(Overflow));

  // Notes on the sheet:
  //   I: pull=down
  //   Overflow: pull=down
  //   S: pull=down
endmodule
