// Logisim project 20BitBitwiseOr.circ as structural Verilog: 1 circuit, main circuit 20BitBitwiseOr
module _20BitBitwiseOr (
  input  [19:0] I0,
  input  [19:0] I1,
  output [19:0] S
);

  or or_1 (S[0], I0[0], I1[0]);
  or or_2 (S[19], I0[19], I1[19]);
  or or_3 (S[1], I0[1], I1[1]);
  or or_4 (S[2], I0[2], I1[2]);
  or or_5 (S[17], I0[17], I1[17]);
  or or_6 (S[18], I0[18], I1[18]);
  or or_7 (S[4], I0[4], I1[4]);
  or or_8 (S[3], I0[3], I1[3]);
  or or_9 (S[15], I0[15], I1[15]);
  or or_10 (S[16], I0[16], I1[16]);
  or or_11 (S[6], I0[6], I1[6]);
  or or_12 (S[5], I0[5], I1[5]);
  or or_13 (S[13], I0[13], I1[13]);
  or or_14 (S[14], I0[14], I1[14]);
  or or_15 (S[7], I0[7], I1[7]);
  or or_16 (S[8], I0[8], I1[8]);
  or or_17 (S[11], I0[11], I1[11]);
  or or_18 (S[12], I0[12], I1[12]);
  or or_19 (S[9], I0[9], I1[9]);
  or or_20 (S[10], I0[10], I1[10]);

  // Notes on the sheet:
  //   I0: pull=down
  //   I1: pull=down
  //   S: pull=down
endmodule
