// Logisim project 20BitBitwiseXor.circ as structural Verilog: 1 circuit, main circuit 20BitBitwiseXor
module _20BitBitwiseXor (
  input  [19:0] N0,
  input  [19:0] N1,
  output [19:0] R
);

  xor xor_1 (R[0], N0[0], N1[0]);
  xor xor_2 (R[19], N0[19], N1[19]);
  xor xor_3 (R[2], N0[2], N1[2]);
  xor xor_4 (R[1], N0[1], N1[1]);
  xor xor_5 (R[18], N0[18], N1[18]);
  xor xor_6 (R[17], N0[17], N1[17]);
  xor xor_7 (R[3], N0[3], N1[3]);
  xor xor_8 (R[4], N0[4], N1[4]);
  xor xor_9 (R[15], N0[15], N1[15]);
  xor xor_10 (R[16], N0[16], N1[16]);
  xor xor_11 (R[6], N0[6], N1[6]);
  xor xor_12 (R[5], N0[5], N1[5]);
  xor xor_13 (R[14], N0[14], N1[14]);
  xor xor_14 (R[13], N0[13], N1[13]);
  xor xor_15 (R[7], N0[7], N1[7]);
  xor xor_16 (R[8], N0[8], N1[8]);
  xor xor_17 (R[11], N0[11], N1[11]);
  xor xor_18 (R[12], N0[12], N1[12]);
  xor xor_19 (R[9], N0[9], N1[9]);
  xor xor_20 (R[10], N0[10], N1[10]);

  // Notes on the sheet:
  //   N0: pull=down
  //   N1: pull=down
  //   R: pull=down
endmodule
