// Logisim project CPU.circ as structural Verilog: 1 circuit, main circuit CPU
module CPU (
);

  wire BE_Select, BEQ, clk, Cout, Fetch, Imm, MemWrite, PC_Overflow, PCR_Select, PCRead, PCW_Select, PCWrite,
       RegW_Select, RegWrite, zero;
  wire [3:0] Dr, Sr1, Sr2;
  wire [9:0] Addr, multiplexer_1_out, multiplexer_2_out, n10bitdecrementer_1_s, PC;
  wire [19:0] ALQ, bit_extender_1_out, Imm_Offset, Inst, MemQ, multiplexer_3_out, multiplexer_4_out,
       multiplexer_5_out, R1, R2;

  Multiplexer #(.width(10), .disabled(0), .enable("false")) multiplexer_1 (
    .in0(PC), .in1(Addr), .out(multiplexer_1_out), .sel(BEQ));
  Multiplexer #(.width(10), .disabled(0), .enable("false")) multiplexer_2 (
    .in0(ALQ[9:0]), .in1(multiplexer_1_out), .out(multiplexer_2_out), .sel(PCW_Select));
  Memory memory_1 (.clk(clk), .WR_Select(MemWrite), .A(Addr), .D(R1), .D_2(MemQ), .PC(PC), .Inst(Inst), .reset(zero));
  ProgramCounter programcounter_1 (
    .Addr(multiplexer_2_out), .Fetch(Fetch), .PCWrite(PCWrite), .clk(clk), .t_0(zero),
    .PC_Overflow(PC_Overflow), .PC(PC));
  Clock clock_1 (.clk(clk), .t_0(zero));
  _10BitDecrementer u_10bitdecrementer_1 (.I(PC), .S(n10bitdecrementer_1_s));  // open: Overflow
  assign bit_extender_1_out = {{10{1'b0}}, n10bitdecrementer_1_s};  // Bit_Extender bit_extender_1
  Multiplexer #(.width(20), .disabled(0), .enable("false")) multiplexer_3 (
    .in0(R1), .in1(bit_extender_1_out), .out(multiplexer_3_out), .sel(PCR_Select));
  Multiplexer #(.width(20), .disabled(0), .enable("false")) multiplexer_4 (
    .in0(R2), .in1(Imm_Offset), .out(multiplexer_4_out), .sel(Imm));
  // Control_Unit Control_Unit: pin names not known; wires that end beside it: PCRead, PCWrite, Imm, RegW_Select, PCR_Select, PCW_Select, BE_Select
  // ALU alu_1: pin names not known; wires that end beside it: Cout, BE_Select, ALQ, BEQ
  Multiplexer #(.width(20), .disabled(0), .enable("false")) multiplexer_5 (
    .in0(MemQ), .in1(ALQ), .out(multiplexer_5_out), .sel(RegW_Select));
  // RegisterFile registerfile_1: pin names not known; wires that end beside it: Sr1, Sr2, RegWrite, clk, multiplexer_5_out, zero, Dr, R1, R2
endmodule
