// Logisim project Terminator.circ as structural Verilog: 1 circuit, main circuit Terminator
module Terminator (
  input  clk,
  input  t_0,
  input  Decode,
  input  Halt_Instruction,
  input  Stack_Overflow,
  input  Instruction_End,
  input  PC_Overflow,
  output Halted
);

  wire and_1_out, and_2_out, Delay_q, Halted_p4, or_1_out, PCOverflowed_p4, risingedgetriggereddflipflop_1_p4;

  // RisingEdgeTriggeredDFlipFlop risingedgetriggereddflipflop_1: pin names not known; wires that end beside it: Decode, clk, t_0, risingedgetriggereddflipflop_1_p4
  // RisingEdgeTriggeredDFlipFlop PCOverflowed: pin names not known; wires that end beside it: PC_Overflow, clk, t_0, PCOverflowed_p4
  and and_1 (and_1_out, risingedgetriggereddflipflop_1_p4, Halt_Instruction);
  and and_2 (and_2_out, Instruction_End, PCOverflowed_p4);
  FallingEdgeTriggeredDFlipFlop Delay (.D(1'b1), .C(and_2_out), .Q(Delay_q));
  or or_1 (or_1_out, and_1_out, Stack_Overflow, Delay_q);
  // RisingEdgeTriggeredDFlipFlop Halted: pin names not known; wires that end beside it: or_1_out, or_1_out, t_0, Halted_p4
  or or_2 (Halted, Halted_p4, or_1_out);

  // Notes on the sheet:
  //   Stack_Overflow: pull=down
  //   PC_Overflow: pull=down
  //   t_0: pull=down
  //   clk: pull=down
  //   Halted: pull=down
  //   Instruction_End: pull=down
  //   Decode: pull=down
  //   Halt_Instruction: pull=down
endmodule
