// Logisim project FallingEdgeTriggeredDFlipFlop.circ as structural Verilog: 1 circuit, main circuit FallingEdgeTriggeredDFlipFlop
module FallingEdgeTriggeredDFlipFlop (
  input  D,
  input  W_Enable,
  input  clk,
  output Q
);

  wire dlatch_1_q, multiplexer_1_out, not_1_out;

  Multiplexer #(.enable("false")) multiplexer_1 (.in0(Q), .in1(D), .out(multiplexer_1_out), .sel(W_Enable));
  DLatch dlatch_1 (.D(multiplexer_1_out), .C(clk), .Q(dlatch_1_q));
  not not_1 (not_1_out, clk);
  DLatch dlatch_2 (.D(dlatch_1_q), .C(not_1_out), .Q(Q));

  // Notes on the sheet:
  //   W_Enable: pull=down
  //   D: pull=down
  //   clk: pull=down
  //   Q: pull=down
endmodule
