// Logisim project RisingEdgeTriggeredDFlipFlop.circ as structural Verilog: 1 circuit, main circuit RisingEdgeTriggeredDFlipFlop
module RisingEdgeTriggeredDFlipFlop (
  input  D,
  input  W_Enable,
  input  clk,
  input  reset,
  output Q
);

  wire dlatch_1_q, multiplexer_1_out, not_1_out;

  Multiplexer #(.enable("false")) multiplexer_1 (.in0(Q), .in1(D), .out(multiplexer_1_out), .sel(W_Enable));
  not not_1 (not_1_out, clk);
  DLatch dlatch_1 (.D(multiplexer_1_out), .clk(not_1_out), .Q(dlatch_1_q), .clr(1'b0));
  DLatch dlatch_2 (.D(dlatch_1_q), .clk(clk), .Q(Q), .clr(reset));

  // Notes on the sheet:
  //   D: pull=down
  //   clk: pull=down
  //   Q: pull=down
  //   reset: pull=down
  //   W_Enable: pull=down
endmodule
