// Logisim project Memory.circ as structural Verilog: 1 circuit, main circuit Memory
module Memory (
  input  [9:0] A,
  input  [19:0] D,
  input  clk,
  input  Mem_Select,
  input  WR_Select,
  output [19:0] D_2
);

  wire not_1_out, not_2_out;
  wire [19:0] ram_1_data, ram_2_data;

  not not_1 (not_1_out, Mem_Select);
  not not_2 (not_2_out, WR_Select);
  RAM #(.addrWidth(10), .dataWidth(20), .bus("separate")) ram_1 (
    .addr(A), .din(D), .data(ram_1_data), .str(WR_Select), .sel(not_1_out), .clk(clk), .ld(not_2_out));  // open: clr
  Multiplexer #(.width(20), .disabled(0), .enable("false")) multiplexer_1 (
    .in0(ram_1_data), .in1(ram_2_data), .out(D_2), .sel(Mem_Select));
  RAM #(.addrWidth(10), .dataWidth(20), .bus("separate")) ram_2 (
    .addr(A), .din(D), .data(ram_2_data), .str(WR_Select), .sel(Mem_Select), .clk(clk), .ld(not_2_out));  // open: clr

  // Notes on the sheet:
  //   clk: pull=down
  //   A: pull=down
  //   WR_Select: pull=down
  //   Mem_Select: pull=down
  //   D: pull=down
  //   D_2: pull=down
  //   Data Memory
  //   Instruction Memory
endmodule
