// Logisim project 3BitRegister.circ as structural Verilog: 1 circuit, main circuit 3BitRegister
module _3BitRegister (
  input  [2:0] in_1,
  input  C,
  input  E,
  output [2:0] out_4
);

  RisingEdgeTriggeredDFlipFlop risingedgetriggereddflipflop_1 (.D(in_1[2]), .clk(C), .Q(out_4[2]), .W_Enable(E));
  RisingEdgeTriggeredDFlipFlop risingedgetriggereddflipflop_2 (.D(in_1[1]), .clk(C), .Q(out_4[1]), .W_Enable(E));
  RisingEdgeTriggeredDFlipFlop risingedgetriggereddflipflop_3 (.D(in_1[0]), .clk(C), .Q(out_4[0]), .W_Enable(E));

  // Notes on the sheet:
  //   out_4: pull=down
  //   in_1: pull=down
  //   C: pull=down
  //   E: pull=down
endmodule
