// Logisim project RegisterFile.circ as structural Verilog: 1 circuit, main circuit RegisterFile
module RegisterFile (
  input  [3:0] W_Select,
  input  [19:0] W,
  input  W_Enabled,
  input  clk,
  input  reset,
  input  [3:0] R1_Select,
  input  [3:0] R2_Select,
  output [19:0] R1,
  output [19:0] R2
);

  wire and_1_out, and_2_out, and_3_out, and_4_out, and_5_out, and_6_out, and_7_out, and_8_out, and_9_out,
       and_10_out, and_11_out, and_12_out, and_13_out, and_14_out, and_15_out, and_16_out, decoder_1_out0,
       decoder_1_out1, decoder_1_out2, decoder_1_out3, decoder_1_out4, decoder_1_out5, decoder_1_out6,
       decoder_1_out7, decoder_1_out8, decoder_1_out9, decoder_1_out10, decoder_1_out11, decoder_1_out12,
       decoder_1_out13, decoder_1_out14, decoder_1_out15, decoder_2_out0, decoder_2_out1, decoder_2_out2,
       decoder_2_out3, decoder_2_out4, decoder_2_out5, decoder_2_out6, decoder_2_out7, decoder_2_out8,
       decoder_2_out9, decoder_2_out10, decoder_2_out11, decoder_2_out12, decoder_2_out13, decoder_2_out14,
       decoder_2_out15, decoder_3_out0, decoder_3_out1, decoder_3_out2, decoder_3_out3, decoder_3_out4,
       decoder_3_out5, decoder_3_out6, decoder_3_out7, decoder_3_out8, decoder_3_out9, decoder_3_out10,
       decoder_3_out11, decoder_3_out12, decoder_3_out13, decoder_3_out14, decoder_3_out15;
  wire [19:0] n20bitregister_1_p5, n20bitregister_2_p5, n20bitregister_3_p5, n20bitregister_4_p5,
       n20bitregister_5_p5, n20bitregister_6_p5, n20bitregister_7_p5, n20bitregister_8_p5,
       n20bitregister_9_p5, n20bitregister_10_p5, n20bitregister_11_p5, n20bitregister_12_p5,
       n20bitregister_13_p5, n20bitregister_14_p5, n20bitregister_15_p5, n20bitregister_16_p5;

  and and_1 (and_1_out, decoder_2_out0, W_Enabled);
  assign R1 = decoder_1_out0 ? n20bitregister_1_p5 : 20'bz;  // Controlled_Buffer controlled_buffer_1
  and and_2 (and_2_out, decoder_2_out1, W_Enabled);
  // _20BitRegister 20bitregister_1: pin names not known; wires that end beside it: and_1_out, clk, reset, W, n20bitregister_1_p5
  assign R2 = decoder_3_out0 ? n20bitregister_1_p5 : 20'bz;  // Controlled_Buffer controlled_buffer_2
  // _20BitRegister 20bitregister_2: pin names not known; wires that end beside it: and_2_out, clk, reset, W, n20bitregister_2_p5
  assign R2 = decoder_3_out1 ? n20bitregister_2_p5 : 20'bz;  // Controlled_Buffer controlled_buffer_3
  assign R1 = decoder_1_out1 ? n20bitregister_2_p5 : 20'bz;  // Controlled_Buffer controlled_buffer_4
  and and_3 (and_3_out, decoder_2_out2, W_Enabled);
  assign R1 = decoder_1_out2 ? n20bitregister_3_p5 : 20'bz;  // Controlled_Buffer controlled_buffer_5
  and and_4 (and_4_out, decoder_2_out3, W_Enabled);
  // _20BitRegister 20bitregister_3: pin names not known; wires that end beside it: and_3_out, clk, reset, W, n20bitregister_3_p5
  assign R2 = decoder_3_out2 ? n20bitregister_3_p5 : 20'bz;  // Controlled_Buffer controlled_buffer_6
  // _20BitRegister 20bitregister_4: pin names not known; wires that end beside it: and_4_out, clk, reset, W, n20bitregister_4_p5
  assign R2 = decoder_3_out3 ? n20bitregister_4_p5 : 20'bz;  // Controlled_Buffer controlled_buffer_7
  assign R1 = decoder_1_out3 ? n20bitregister_4_p5 : 20'bz;  // Controlled_Buffer controlled_buffer_8
  and and_5 (and_5_out, decoder_2_out4, W_Enabled);
  assign R1 = decoder_1_out4 ? n20bitregister_5_p5 : 20'bz;  // Controlled_Buffer controlled_buffer_9
  and and_6 (and_6_out, decoder_2_out5, W_Enabled);
  // _20BitRegister 20bitregister_5: pin names not known; wires that end beside it: and_5_out, clk, reset, W, n20bitregister_5_p5
  assign R2 = decoder_3_out4 ? n20bitregister_5_p5 : 20'bz;  // Controlled_Buffer controlled_buffer_10
  // _20BitRegister 20bitregister_6: pin names not known; wires that end beside it: and_6_out, clk, reset, W, n20bitregister_6_p5
  assign R2 = decoder_3_out5 ? n20bitregister_6_p5 : 20'bz;  // Controlled_Buffer controlled_buffer_11
  assign R1 = decoder_1_out5 ? n20bitregister_6_p5 : 20'bz;  // Controlled_Buffer controlled_buffer_12
  and and_7 (and_7_out, decoder_2_out6, W_Enabled);
  assign R1 = decoder_1_out6 ? n20bitregister_7_p5 : 20'bz;  // Controlled_Buffer controlled_buffer_13
  and and_8 (and_8_out, decoder_2_out7, W_Enabled);
  // _20BitRegister 20bitregister_7: pin names not known; wires that end beside it: and_7_out, clk, reset, W, n20bitregister_7_p5
  assign R2 = decoder_3_out6 ? n20bitregister_7_p5 : 20'bz;  // Controlled_Buffer controlled_buffer_14
  Decoder #(.select(4), .disabled(0), .enable("false")) decoder_1 (
    .out0(decoder_1_out0), .out1(decoder_1_out1), .out2(decoder_1_out2), .out3(decoder_1_out3),
    .out4(decoder_1_out4), .out5(decoder_1_out5), .out6(decoder_1_out6), .out7(decoder_1_out7),
    .out8(decoder_1_out8), .out9(decoder_1_out9), .out10(decoder_1_out10), .out11(decoder_1_out11),
    .out12(decoder_1_out12), .out13(decoder_1_out13), .out14(decoder_1_out14), .out15(decoder_1_out15),
    .sel(R1_Select));
  Decoder #(.select(4), .disabled(0), .enable("false")) decoder_2 (
    .out0(decoder_2_out0), .out1(decoder_2_out1), .out2(decoder_2_out2), .out3(decoder_2_out3),
    .out4(decoder_2_out4), .out5(decoder_2_out5), .out6(decoder_2_out6), .out7(decoder_2_out7),
    .out8(decoder_2_out8), .out9(decoder_2_out9), .out10(decoder_2_out10), .out11(decoder_2_out11),
    .out12(decoder_2_out12), .out13(decoder_2_out13), .out14(decoder_2_out14), .out15(decoder_2_out15),
    .sel(W_Select));
  // _20BitRegister 20bitregister_8: pin names not known; wires that end beside it: and_8_out, clk, reset, W, n20bitregister_8_p5
  assign R2 = decoder_3_out7 ? n20bitregister_8_p5 : 20'bz;  // Controlled_Buffer controlled_buffer_15
  assign R1 = decoder_1_out7 ? n20bitregister_8_p5 : 20'bz;  // Controlled_Buffer controlled_buffer_16
  and and_9 (and_9_out, decoder_2_out8, W_Enabled);
  assign R1 = decoder_1_out8 ? n20bitregister_9_p5 : 20'bz;  // Controlled_Buffer controlled_buffer_17
  and and_10 (and_10_out, decoder_2_out9, W_Enabled);
  // _20BitRegister 20bitregister_9: pin names not known; wires that end beside it: and_9_out, clk, reset, W, n20bitregister_9_p5
  assign R2 = decoder_3_out8 ? n20bitregister_9_p5 : 20'bz;  // Controlled_Buffer controlled_buffer_18
  // _20BitRegister 20bitregister_10: pin names not known; wires that end beside it: and_10_out, clk, reset, W, n20bitregister_10_p5
  assign R1 = decoder_1_out9 ? n20bitregister_10_p5 : 20'bz;  // Controlled_Buffer controlled_buffer_19
  assign R2 = decoder_3_out9 ? n20bitregister_10_p5 : 20'bz;  // Controlled_Buffer controlled_buffer_20
  Decoder #(.select(4), .disabled(0), .enable("false")) decoder_3 (
    .out0(decoder_3_out0), .out1(decoder_3_out1), .out2(decoder_3_out2), .out3(decoder_3_out3),
    .out4(decoder_3_out4), .out5(decoder_3_out5), .out6(decoder_3_out6), .out7(decoder_3_out7),
    .out8(decoder_3_out8), .out9(decoder_3_out9), .out10(decoder_3_out10), .out11(decoder_3_out11),
    .out12(decoder_3_out12), .out13(decoder_3_out13), .out14(decoder_3_out14), .out15(decoder_3_out15),
    .sel(R2_Select));
  and and_11 (and_11_out, decoder_2_out10, W_Enabled);
  assign R1 = decoder_1_out10 ? n20bitregister_11_p5 : 20'bz;  // Controlled_Buffer controlled_buffer_21
  and and_12 (and_12_out, decoder_2_out11, W_Enabled);
  // _20BitRegister 20bitregister_11: pin names not known; wires that end beside it: and_11_out, clk, reset, W, n20bitregister_11_p5
  assign R2 = decoder_3_out10 ? n20bitregister_11_p5 : 20'bz;  // Controlled_Buffer controlled_buffer_22
  // _20BitRegister 20bitregister_12: pin names not known; wires that end beside it: and_12_out, clk, reset, W, n20bitregister_12_p5
  assign R2 = decoder_3_out11 ? n20bitregister_12_p5 : 20'bz;  // Controlled_Buffer controlled_buffer_23
  assign R1 = decoder_1_out11 ? n20bitregister_12_p5 : 20'bz;  // Controlled_Buffer controlled_buffer_24
  and and_13 (and_13_out, decoder_2_out12, W_Enabled);
  assign R1 = decoder_1_out12 ? n20bitregister_13_p5 : 20'bz;  // Controlled_Buffer controlled_buffer_25
  and and_14 (and_14_out, decoder_2_out13, W_Enabled);
  // _20BitRegister 20bitregister_13: pin names not known; wires that end beside it: and_13_out, clk, reset, W, n20bitregister_13_p5
  assign R2 = decoder_3_out12 ? n20bitregister_13_p5 : 20'bz;  // Controlled_Buffer controlled_buffer_26
  // _20BitRegister 20bitregister_14: pin names not known; wires that end beside it: and_14_out, clk, reset, W, n20bitregister_14_p5
  assign R1 = decoder_1_out13 ? n20bitregister_14_p5 : 20'bz;  // Controlled_Buffer controlled_buffer_27
  assign R2 = decoder_3_out13 ? n20bitregister_14_p5 : 20'bz;  // Controlled_Buffer controlled_buffer_28
  and and_15 (and_15_out, decoder_2_out14, W_Enabled);
  assign R1 = decoder_1_out14 ? n20bitregister_15_p5 : 20'bz;  // Controlled_Buffer controlled_buffer_29
  and and_16 (and_16_out, decoder_2_out15, W_Enabled);
  // _20BitRegister 20bitregister_15: pin names not known; wires that end beside it: and_15_out, clk, reset, W, n20bitregister_15_p5
  assign R2 = decoder_3_out14 ? n20bitregister_15_p5 : 20'bz;  // Controlled_Buffer controlled_buffer_30
  // _20BitRegister 20bitregister_16: pin names not known; wires that end beside it: and_16_out, clk, reset, W, n20bitregister_16_p5
  assign R2 = decoder_3_out15 ? n20bitregister_16_p5 : 20'bz;  // Controlled_Buffer controlled_buffer_31
  assign R1 = decoder_1_out15 ? n20bitregister_16_p5 : 20'bz;  // Controlled_Buffer controlled_buffer_32

  // Notes on the sheet:
  //   R1: pull=down
  //   clk: pull=down
  //   R2_Select: pull=down
  //   R1_Select: pull=down
  //   W_Enabled: pull=down
  //   W: pull=down
  //   R2: pull=down
  //   W_Select: pull=down
  //   reset: pull=down
endmodule
