// Logisim project 20BitSubtractor.circ as structural Verilog: 1 circuit, main circuit 20BitSubtractor
module _20BitSubtractor (
  input  [19:0] I0,
  input  [19:0] I1,
  output B_out,
  output [19:0] D
);

  wire fullsubtractor_2_bout, fullsubtractor_3_bout, fullsubtractor_4_bout, fullsubtractor_5_bout,
       fullsubtractor_6_bout, fullsubtractor_7_bout, fullsubtractor_8_bout, fullsubtractor_9_bout,
       fullsubtractor_10_bout, fullsubtractor_11_bout, fullsubtractor_12_bout, fullsubtractor_13_bout,
       fullsubtractor_14_bout, fullsubtractor_15_bout, fullsubtractor_16_bout, fullsubtractor_17_bout,
       fullsubtractor_18_bout, fullsubtractor_19_bout, halfsubtractor_1_b;

  HalfSubtractor halfsubtractor_1 (.N0(I0[0]), .N1(I1[0]), .D(D[0]), .B(halfsubtractor_1_b));
  FullSubtractor fullsubtractor_1 (.N0(I0[19]), .N1(I1[19]), .Bin(fullsubtractor_3_bout), .D(D[19]), .Bout(B_out));
  FullSubtractor fullsubtractor_2 (
    .N0(I0[1]), .N1(I1[1]), .Bin(halfsubtractor_1_b), .D(D[1]), .Bout(fullsubtractor_2_bout));
  FullSubtractor fullsubtractor_3 (
    .N0(I0[18]), .N1(I1[18]), .Bin(fullsubtractor_5_bout), .D(D[18]), .Bout(fullsubtractor_3_bout));
  FullSubtractor fullsubtractor_4 (
    .N0(I0[2]), .N1(I1[2]), .Bin(fullsubtractor_2_bout), .D(D[2]), .Bout(fullsubtractor_4_bout));
  FullSubtractor fullsubtractor_5 (
    .N0(I0[17]), .N1(I1[17]), .Bin(fullsubtractor_7_bout), .D(D[17]), .Bout(fullsubtractor_5_bout));
  FullSubtractor fullsubtractor_6 (
    .N0(I0[3]), .N1(I1[3]), .Bin(fullsubtractor_4_bout), .D(D[3]), .Bout(fullsubtractor_6_bout));
  FullSubtractor fullsubtractor_7 (
    .N0(I0[16]), .N1(I1[16]), .Bin(fullsubtractor_11_bout), .D(D[16]), .Bout(fullsubtractor_7_bout));
  FullSubtractor fullsubtractor_8 (
    .N0(I0[5]), .N1(I1[5]), .Bin(fullsubtractor_9_bout), .D(D[5]), .Bout(fullsubtractor_8_bout));
  FullSubtractor fullsubtractor_9 (
    .N0(I0[4]), .N1(I1[4]), .Bin(fullsubtractor_6_bout), .D(D[4]), .Bout(fullsubtractor_9_bout));
  FullSubtractor fullsubtractor_10 (
    .N0(I0[14]), .N1(I1[14]), .Bin(fullsubtractor_13_bout), .D(D[14]), .Bout(fullsubtractor_10_bout));
  FullSubtractor fullsubtractor_11 (
    .N0(I0[15]), .N1(I1[15]), .Bin(fullsubtractor_10_bout), .D(D[15]), .Bout(fullsubtractor_11_bout));
  FullSubtractor fullsubtractor_12 (
    .N0(I0[6]), .N1(I1[6]), .Bin(fullsubtractor_8_bout), .D(D[6]), .Bout(fullsubtractor_12_bout));
  FullSubtractor fullsubtractor_13 (
    .N0(I0[13]), .N1(I1[13]), .Bin(fullsubtractor_15_bout), .D(D[13]), .Bout(fullsubtractor_13_bout));
  FullSubtractor fullsubtractor_14 (
    .N0(I0[7]), .N1(I1[7]), .Bin(fullsubtractor_12_bout), .D(D[7]), .Bout(fullsubtractor_14_bout));
  FullSubtractor fullsubtractor_15 (
    .N0(I0[12]), .N1(I1[12]), .Bin(fullsubtractor_17_bout), .D(D[12]), .Bout(fullsubtractor_15_bout));
  FullSubtractor fullsubtractor_16 (
    .N0(I0[8]), .N1(I1[8]), .Bin(fullsubtractor_14_bout), .D(D[8]), .Bout(fullsubtractor_16_bout));
  FullSubtractor fullsubtractor_17 (
    .N0(I0[11]), .N1(I1[11]), .Bin(fullsubtractor_19_bout), .D(D[11]), .Bout(fullsubtractor_17_bout));
  FullSubtractor fullsubtractor_18 (
    .N0(I0[9]), .N1(I1[9]), .Bin(fullsubtractor_16_bout), .D(D[9]), .Bout(fullsubtractor_18_bout));
  FullSubtractor fullsubtractor_19 (
    .N0(I0[10]), .N1(I1[10]), .Bin(fullsubtractor_18_bout), .D(D[10]), .Bout(fullsubtractor_19_bout));

  // Notes on the sheet:
  //   D: pull=down
  //   I1: pull=down
  //   B_out: pull=down
  //   I0: pull=down
endmodule
