// Logisim project FullSubtractor.circ as structural Verilog: 1 circuit, main circuit FullSubtractor
module FullSubtractor (
  input  I0,
  input  I1,
  input  B_in,
  output D,
  output B_out
);

  wire halfsubtractor_1_b, halfsubtractor_1_d, halfsubtractor_2_b;

  HalfSubtractor halfsubtractor_1 (.N0(I0), .N1(I1), .D(halfsubtractor_1_d), .B(halfsubtractor_1_b));
  HalfSubtractor halfsubtractor_2 (.N0(halfsubtractor_1_d), .N1(B_in), .D(D), .B(halfsubtractor_2_b));
  or or_1 (B_out, halfsubtractor_2_b, halfsubtractor_1_b);

  // Notes on the sheet:
  //   B_out: pull=down
  //   B_in: pull=down
  //   I0: pull=down
  //   D: pull=down
  //   I1: pull=down
endmodule
