// Logisim project HalfSubtractor.circ as structural Verilog: 1 circuit, main circuit HalfSubtractor
module HalfSubtractor (
  input  N0,
  input  N1,
  output D,
  output B
);

  wire not_1_out;

  xor xor_1 (D, N0, N1);
  and and_1 (B, N1, not_1_out);
  not not_1 (not_1_out, N0);

  // Notes on the sheet:
  //   N0: pull=down
  //   N1: pull=down
  //   D: pull=down
  //   B: pull=down
endmodule
